// Digital circuit example.dig as structural Verilog
module example (
  input  in_1,
  input  in_2,
  input  in_3,
  input  in_4,
  input  in_6,
  input  in_7,
  input  in_8,
  input  in_9,
  output out_5,
  output out_10
);

  wire and_1_out, and_2_out, and_3_out, and_4_out;

  and and_1 (and_1_out, in_1, in_2);
  and and_2 (and_2_out, in_3, in_4);
  and and_3 (and_3_out, in_6, in_7);
  and and_4 (and_4_out, in_8, in_9);
  or or_1 (out_5, and_1_out, and_2_out);
  or or_2 (out_10, and_3_out, and_4_out);
endmodule
